// Logisim project 8_bit_CPU.circ as structural Verilog: 10 circuits, main circuit main
module main (
  output [7:0] out_1,
  output [15:0] out_2,
  output [7:0] out_3,
  output [7:0] out_4
);

  wire button_1_out, button_2_out, button_3_out, button_4_out, clock_1_out, d_ff_1_q, d_ff_1_qn, d_ff_2_q,
       d_ff_2_qn, d_ff_3_q, d_ff_3_qn, d_ff_4_q, d_ff_4_qn, d_ff_5_q, d_ff_5_qn, d_ff_6_q, d_ff_6_qn,
       nand_1_out, not_1_out, not_2_out, not_3_out, or_1_out, register_8bit_2_borrow, register_8bit_2_carry,
       RESET_out, undriven_3, undriven_5;
  wire [7:0] ring_counter_1_q, undriven, undriven_2, undriven_4;

  Button #(.press("passive")) button_1 (.out(button_1_out));
  Clock clock_1 (.out(clock_1_out));
  Button RESET (.out(RESET_out));
  not not_1 (not_1_out, button_1_out);
  nand nand_1 (nand_1_out, button_1_out, not_1_out);
  register_8bit register_8bit_1 (
    .DATA(undriven_2), .NOT_WRITE(1'b1), .RESET(RESET_out), .INC(register_8bit_2_carry),
    .DEC(register_8bit_2_borrow), .Q(out_2[15:8]));  // open: CARRY, BORROW
  or or_1 (or_1_out, ring_counter_1_q[6], ring_counter_1_q[4]);
  Button #(.press("passive")) button_2 (.out(button_2_out));
  Button #(.press("passive")) button_3 (.out(button_3_out));
  Button #(.press("passive")) button_4 (.out(button_4_out));
  register_8bit register_8bit_2 (
    .DATA(undriven), .NOT_WRITE(1'b1), .RESET(RESET_out), .INC(or_1_out), .DEC(1'b1), .Q(out_2[7:0]),
    .CARRY(register_8bit_2_carry), .BORROW(register_8bit_2_borrow));
  register_8bit register_8bit_3 (
    .DATA(8'h80), .NOT_WRITE(button_2_out), .INC(button_3_out), .DEC(button_4_out), .Q(out_3));  // open: RESET, CARRY, BORROW
  ring_counter ring_counter_1 (.CLK(clock_1_out), .RESET(RESET_out), .Q(ring_counter_1_q));
  adder_subtractor_8bit adder_subtractor_8bit_1 (.A(8'h2), .B(8'hf0), .SUBTRACT(undriven_3), .Q(out_4));  // open: C_OUT
  ALU alu_1 ();  // open: OVERFLOW_SET, OVERFLOW_RESET, CARRY_RESET, CARRY_SET, WRITE_FLAGS, MODIFIER, ALU_OPERAND, ACC_NOT_WRITE, RESET, INC, DEC, ACC_OUT_DISABLE, ACC_IN_ENABLE, ACC_INPUT, OP_SELECT, OFL, CFL, ACC_OUT, AF0, AF1, AF2, AF3, ZFL, AF4, AF5, AF6, NFL
  D_Flip_Flop d_ff_1 (.D(d_ff_1_qn), .Q(d_ff_1_q), .Qn(d_ff_1_qn), .reset(undriven_5));  // open: clk, preset
  not not_2 (not_2_out, ring_counter_1_q[7]);
  not not_3 (not_3_out, ring_counter_1_q[5]);
  D_Flip_Flop d_ff_2 (
    .D(d_ff_2_qn), .clk(d_ff_1_qn), .Q(d_ff_2_q), .Qn(d_ff_2_qn), .reset(undriven_5));  // open: preset
  D_Flip_Flop d_ff_3 (
    .D(d_ff_3_qn), .clk(d_ff_2_qn), .Q(d_ff_3_q), .Qn(d_ff_3_qn), .reset(undriven_5));  // open: preset
  D_Flip_Flop d_ff_4 (
    .D(d_ff_4_qn), .clk(d_ff_3_qn), .Q(d_ff_4_q), .Qn(d_ff_4_qn), .reset(undriven_5));  // open: preset
  register_8bit OPCODE_REGISTER (
    .DATA(undriven_4), .NOT_WRITE(not_2_out), .RESET(RESET_out));  // open: INC, DEC, Q, CARRY, BORROW
  register_8bit OPERAND_REGISTER (
    .DATA(undriven_4), .NOT_WRITE(not_3_out), .RESET(RESET_out), .Q(out_1));  // open: INC, DEC, CARRY, BORROW
  D_Flip_Flop d_ff_5 (
    .D(d_ff_5_qn), .clk(d_ff_4_qn), .Q(d_ff_5_q), .Qn(d_ff_5_qn), .reset(undriven_5));  // open: preset
  D_Flip_Flop d_ff_6 (
    .D(d_ff_6_qn), .clk(d_ff_5_qn), .Q(d_ff_6_q), .Qn(d_ff_6_qn), .reset(undriven_5));  // open: preset
  D_Flip_Flop IRQ_DISABLE_FLAG ();  // open: D, clk, Q, Qn, preset, reset

  // Notes on the sheet:
  //   PROGRAM COUNTER
endmodule

module register_8bit (
  input  [7:0] DATA,
  input  NOT_WRITE,
  input  RESET,
  input  INC,
  input  DEC,
  output [7:0] Q,
  output CARRY,
  output BORROW
);

  wire n74193_1_pin4, n74193_1_pin5;

  _74193 #(.ShowInternalStructure("true")) u_74193_1 (
    .pin1(DATA[5]), .pin2(Q[5]), .pin3(Q[4]), .pin4(n74193_1_pin4), .pin5(n74193_1_pin5), .pin6(Q[6]),
    .pin7(Q[7]), .pin15(DATA[4]), .pin14(RESET), .pin13(BORROW), .pin12(CARRY), .pin11(NOT_WRITE),
    .pin10(DATA[6]), .pin9(DATA[7]));
  _74193 #(.ShowInternalStructure("true")) u_74193_2 (
    .pin1(DATA[1]), .pin2(Q[1]), .pin3(Q[0]), .pin4(DEC), .pin5(INC), .pin6(Q[2]), .pin7(Q[3]),
    .pin15(DATA[0]), .pin14(RESET), .pin13(n74193_1_pin4), .pin12(n74193_1_pin5), .pin11(NOT_WRITE),
    .pin10(DATA[2]), .pin9(DATA[3]));
endmodule

module ring_counter (
  input  CLK,
  input  RESET,
  output [7:0] Q
);

  wire nor_1_out, or_1_out, or_2_out, or_3_out, or_4_out, or_5_out, or_6_out;

  D_Flip_Flop d_ff_1 (.D(Q[0]), .clk(CLK), .Q(Q[7]), .preset(nor_1_out), .reset(RESET));  // open: Qn
  or or_1 (or_1_out, Q[7], Q[6]);
  D_Flip_Flop d_ff_2 (.D(Q[7]), .clk(CLK), .Q(Q[6]), .reset(RESET));  // open: Qn, preset
  or or_2 (or_2_out, or_1_out, or_3_out);
  D_Flip_Flop d_ff_3 (.D(Q[6]), .clk(CLK), .Q(Q[5]), .reset(RESET));  // open: Qn, preset
  D_Flip_Flop d_ff_4 (.D(Q[5]), .clk(CLK), .Q(Q[4]), .reset(RESET));  // open: Qn, preset
  nor nor_1 (nor_1_out, or_2_out, or_5_out);
  or or_3 (or_3_out, Q[5], Q[4]);
  D_Flip_Flop d_ff_5 (.D(Q[4]), .clk(CLK), .Q(Q[3]), .reset(RESET));  // open: Qn, preset
  or or_4 (or_4_out, Q[3], Q[2]);
  D_Flip_Flop d_ff_6 (.D(Q[3]), .clk(CLK), .Q(Q[2]), .reset(RESET));  // open: Qn, preset
  or or_5 (or_5_out, or_4_out, or_6_out);
  D_Flip_Flop d_ff_7 (.D(Q[2]), .clk(CLK), .Q(Q[1]), .reset(RESET));  // open: Qn, preset
  or or_6 (or_6_out, Q[1], Q[0]);
  D_Flip_Flop d_ff_8 (.D(Q[1]), .clk(CLK), .Q(Q[0]), .reset(RESET));  // open: Qn, preset
endmodule

module full_adder (
  input  A,
  input  B,
  input  C_IN,
  output Q,
  output C_OUT
);

  wire and_1_out, and_2_out, xor_1_out;

  xor xor_1 (xor_1_out, A, B);
  and and_1 (and_1_out, A, B);
  xor xor_2 (Q, xor_1_out, C_IN);
  and and_2 (and_2_out, xor_1_out, C_IN);
  or or_1 (C_OUT, and_2_out, and_1_out);
endmodule

module adder_subtractor_8bit (
  input  [7:0] A,
  input  [7:0] B,
  input  SUBTRACT,
  output [7:0] Q,
  output C_OUT
);

  wire full_adder_2_c_out, full_adder_3_c_out, full_adder_4_c_out, full_adder_5_c_out, full_adder_6_c_out,
       full_adder_7_c_out, full_adder_8_c_out, xor_1_out, xor_2_out, xor_3_out, xor_4_out, xor_5_out,
       xor_6_out, xor_7_out, xor_8_out;

  xor xor_1 (xor_1_out, B[7], SUBTRACT);
  xor xor_2 (xor_2_out, B[6], SUBTRACT);
  full_adder full_adder_1 (.A(A[7]), .B(xor_1_out), .C_IN(full_adder_2_c_out), .Q(Q[7]), .C_OUT(C_OUT));
  xor xor_3 (xor_3_out, B[5], SUBTRACT);
  full_adder full_adder_2 (.A(A[6]), .B(xor_2_out), .C_IN(full_adder_3_c_out), .Q(Q[6]), .C_OUT(full_adder_2_c_out));
  full_adder full_adder_3 (.A(A[5]), .B(xor_3_out), .C_IN(full_adder_4_c_out), .Q(Q[5]), .C_OUT(full_adder_3_c_out));
  xor xor_4 (xor_4_out, B[4], SUBTRACT);
  xor xor_5 (xor_5_out, B[3], SUBTRACT);
  full_adder full_adder_4 (.A(A[4]), .B(xor_4_out), .C_IN(full_adder_5_c_out), .Q(Q[4]), .C_OUT(full_adder_4_c_out));
  full_adder full_adder_5 (.A(A[3]), .B(xor_5_out), .C_IN(full_adder_6_c_out), .Q(Q[3]), .C_OUT(full_adder_5_c_out));
  xor xor_6 (xor_6_out, B[2], SUBTRACT);
  xor xor_7 (xor_7_out, B[1], SUBTRACT);
  full_adder full_adder_6 (.A(A[2]), .B(xor_6_out), .C_IN(full_adder_7_c_out), .Q(Q[2]), .C_OUT(full_adder_6_c_out));
  full_adder full_adder_7 (.A(A[1]), .B(xor_7_out), .C_IN(full_adder_8_c_out), .Q(Q[1]), .C_OUT(full_adder_7_c_out));
  xor xor_8 (xor_8_out, B[0], SUBTRACT);
  full_adder full_adder_8 (.A(A[0]), .B(xor_8_out), .C_IN(SUBTRACT), .Q(Q[0]), .C_OUT(full_adder_8_c_out));
endmodule

module tri_state_buffer_8bit (
  input  NOT_ENABLE,
  input  [7:0] INPUTS,
  output [7:0] Q
);

  _74244 #(.ShowInternalStructure("true")) u_74244_1 (
    .pin1(NOT_ENABLE), .pin2(INPUTS[4]), .pin3(Q[0]), .pin4(INPUTS[5]), .pin5(Q[1]), .pin6(INPUTS[6]),
    .pin7(Q[2]), .pin8(INPUTS[7]), .pin9(Q[3]), .pin19(NOT_ENABLE), .pin18(Q[4]), .pin17(INPUTS[0]),
    .pin16(Q[5]), .pin15(INPUTS[1]), .pin14(Q[6]), .pin13(INPUTS[2]), .pin12(Q[7]), .pin11(INPUTS[3]));
endmodule

module bit_shifter_right_8bit (
  input  [7:0] DATA,
  input  C_IN,
  output C_OUT,
  output [7:0] Q
);


  assign C_OUT = DATA[0];
  assign Q = {C_IN, DATA[7:1]};
endmodule

module bit_shifter_left_8bit (
  input  C_IN,
  input  [7:0] DATA,
  output [7:0] Q,
  output C_OUT
);


  assign C_OUT = DATA[7];
  assign Q = {DATA[6:0], C_IN};
endmodule

module address_bus (
  input  [15:0] ADDRESS,
  input  WRITE,
  input  [7:0] DATA_IN,
  output [7:0] out_4
);

  wire and_1_out, and_2_out, and_3_out, not_1_out;
  wire [7:0] rom_1_data;

  not not_1 (not_1_out, ADDRESS[14]);
  and and_1 (and_1_out, not_1_out, ADDRESS[15]);
  and and_2 (and_2_out, ADDRESS[15], ADDRESS[14]);
  ROM #(.addrWidth(15)) rom_1 (.addr(ADDRESS[14:0]), .data(rom_1_data));
  RAM #(.addrWidth(14)) ram_1 (
    .addr(ADDRESS[13:0]), .we(1'b1), .oe(and_1_out), .clk(and_3_out), .din(DATA_IN), .dout(out_4));
  and and_3 (and_3_out, and_1_out, WRITE);
  tri_state_buffer_8bit tri_state_buffer_8bit_1 (.NOT_ENABLE(ADDRESS[15]), .INPUTS(rom_1_data), .Q(out_4));

  // Notes on the sheet:
  //   Peripherals, I/O
  //   Add memory locations for interrupt vector table
  //   TODO
  //   Add floating op amp RNG
endmodule

module ALU (
  input  OVERFLOW_SET,
  input  OVERFLOW_RESET,
  input  CARRY_RESET,
  input  CARRY_SET,
  input  WRITE_FLAGS,
  input  MODIFIER,
  input  [7:0] ALU_OPERAND,
  input  ACC_NOT_WRITE,
  input  RESET,
  input  INC,
  input  DEC,
  input  ACC_OUT_DISABLE,
  input  ACC_IN_ENABLE,
  input  [7:0] ACC_INPUT,
  input  [2:0] OP_SELECT,
  output OFL,
  output CFL,
  output [7:0] ACC_OUT,
  output AF0,
  output AF1,
  output AF2,
  output AF3,
  output ZFL,
  output AF4,
  output AF5,
  output AF6,
  output NFL
);

  wire adder_subtractor_8bit_1_c_out, and_1_out, and_2_out, and_4_out, and_5_out, and_6_out, and_7_out,
       and_8_out, and_9_out, and_10_out, bit_shifter_left_8bit_1_c_out, bit_shifter_right_8bit_1_c_out,
       multiplexer_1_out, not_2_out, not_3_out, not_4_out, not_5_out, or_2_out, or_3_out, or_4_out, or_5_out,
       or_6_out, or_7_out, or_8_out, or_9_out, xor_2_out, xor_3_out;
  wire [7:0] adder_subtractor_8bit_1_q, and_3_out, bit_shifter_left_8bit_1_q, bit_shifter_right_8bit_1_q,
       multiplexer_2_out, not_1_out, or_1_out, tri_state_buffer_8bit_1_q, xor_1_out;

  and and_1 (and_1_out, bit_shifter_right_8bit_1_c_out, MODIFIER);
  and and_2 (and_2_out, bit_shifter_left_8bit_1_c_out, MODIFIER);
  assign and_3_out = ALU_OPERAND & {NFL, AF6, AF5, AF4, AF3, AF2, AF1, AF0};  // AND_Gate and_3, 8 bits wide
  assign or_1_out = ALU_OPERAND | {NFL, AF6, AF5, AF4, AF3, AF2, AF1, AF0};  // OR_Gate or_1, 8 bits wide
  assign xor_1_out = ALU_OPERAND ^ {NFL, AF6, AF5, AF4, AF3, AF2, AF1, AF0};  // XOR_Gate xor_1, 8 bits wide
  assign not_1_out = ~ALU_OPERAND;  // NOT_Gate not_1, 8 bits wide
  adder_subtractor_8bit adder_subtractor_8bit_1 (
    .A({NFL, AF6, AF5, AF4, AF3, AF2, AF1, AF0}), .B(ALU_OPERAND), .SUBTRACT(MODIFIER),
    .Q(adder_subtractor_8bit_1_q), .C_OUT(adder_subtractor_8bit_1_c_out));
  bit_shifter_right_8bit bit_shifter_right_8bit_1 (
    .DATA({NFL, AF6, AF5, AF4, AF3, AF2, AF1, AF0}), .C_IN(and_1_out),
    .C_OUT(bit_shifter_right_8bit_1_c_out), .Q(bit_shifter_right_8bit_1_q));
  bit_shifter_left_8bit bit_shifter_left_8bit_1 (
    .C_IN(and_2_out), .DATA({NFL, AF6, AF5, AF4, AF3, AF2, AF1, AF0}), .Q(bit_shifter_left_8bit_1_q),
    .C_OUT(bit_shifter_left_8bit_1_c_out));
  xor xor_2 (xor_2_out, ALU_OPERAND[7], multiplexer_2_out[7]);
  xor xor_3 (xor_3_out, NFL, multiplexer_2_out[7]);
  and and_4 (and_4_out, xor_2_out, xor_3_out);
  Multiplexer #(.select(2)) multiplexer_1 (
    .in0(adder_subtractor_8bit_1_c_out), .in1(bit_shifter_right_8bit_1_c_out),
    .in2(bit_shifter_left_8bit_1_c_out), .out(multiplexer_1_out), .sel(OP_SELECT[1:0]));  // open: in3
  not not_2 (not_2_out, OP_SELECT[0]);
  not not_3 (not_3_out, OP_SELECT[1]);
  not not_4 (not_4_out, OP_SELECT[2]);
  Multiplexer #(.select(3), .width(8)) multiplexer_2 (
    .in0(adder_subtractor_8bit_1_q), .in1(bit_shifter_right_8bit_1_q), .in2(bit_shifter_left_8bit_1_q),
    .in3(and_3_out), .in4(or_1_out), .in5(xor_1_out), .in6(not_1_out), .out(multiplexer_2_out),
    .sel(OP_SELECT));  // open: in7
  and and_5 (and_5_out, WRITE_FLAGS, and_6_out);
  and and_6 (and_6_out, and_7_out, not_4_out);
  and and_7 (and_7_out, not_2_out, not_3_out);
  not not_5 (not_5_out, ACC_IN_ENABLE);
  D_Flip_Flop d_ff_1 (
    .D(and_4_out), .clk(and_5_out), .Q(OFL), .preset(OVERFLOW_SET), .reset(OVERFLOW_RESET));  // open: Qn
  and and_8 (and_8_out, not_2_out, OP_SELECT[1]);
  or or_2 (or_2_out, and_8_out, not_3_out);
  and and_9 (and_9_out, or_2_out, not_4_out);
  tri_state_buffer_8bit tri_state_buffer_8bit_1 (
    .NOT_ENABLE(ACC_IN_ENABLE), .INPUTS(multiplexer_2_out), .Q(tri_state_buffer_8bit_1_q));
  tri_state_buffer_8bit tri_state_buffer_8bit_2 (
    .NOT_ENABLE(not_5_out), .INPUTS(ACC_INPUT), .Q(tri_state_buffer_8bit_1_q));
  D_Flip_Flop CARRY (
    .D(multiplexer_1_out), .clk(and_10_out), .Q(CFL), .preset(CARRY_SET), .reset(or_3_out));  // open: Qn
  and and_10 (and_10_out, WRITE_FLAGS, and_9_out);
  or or_3 (or_3_out, CARRY_RESET, RESET);
  register_8bit ACCUMULATOR (
    .DATA(tri_state_buffer_8bit_1_q), .NOT_WRITE(ACC_NOT_WRITE), .RESET(RESET), .INC(INC), .DEC(DEC),
    .Q({NFL, AF6, AF5, AF4, AF3, AF2, AF1, AF0}));  // open: CARRY, BORROW
  tri_state_buffer_8bit tri_state_buffer_8bit_3 (
    .NOT_ENABLE(ACC_OUT_DISABLE), .INPUTS({NFL, AF6, AF5, AF4, AF3, AF2, AF1, AF0}), .Q(ACC_OUT));
  or or_4 (or_4_out, AF0, AF1);
  or or_5 (or_5_out, AF2, AF3);
  or or_6 (or_6_out, AF4, AF4);
  or or_7 (or_7_out, AF4, NFL);
  or or_8 (or_8_out, or_4_out, or_5_out);
  or or_9 (or_9_out, or_6_out, or_7_out);
  nor nor_1 (ZFL, or_8_out, or_9_out);

  // Notes on the sheet:
  //   ACC_NOT_WRITE: pull=up, initial=0x1
  //   OVERFLOW_SET: pull=down
  //   OVERFLOW_RESET: pull=down
endmodule
